# Fritzing sketch Arduino Memory Connections (saved by Fritzing 0.9.10b)
breadboards: 1

parts:
  Part1 = Arduino Mega ADK (Rev3)
  R1 = Resistor [tolerance=±5% power=0.25 resistance=220 package=THT]
  LED1 = LED - 5mm [color="Red (633nm)" current=30mA package="5 mm [THT]"]
  S1 = Pushbutton [package="[THT]"]
  LED2 = LED - 5mm [color="Yellow (595nm)" current=30mA package="5 mm [THT]"]
  R2 = Resistor [tolerance=±5% power=0.25 resistance=220 package=THT]
  SG1 = Buzzer 12mm [package=buzzer-12mm-ns]
  R3 = Resistor [tolerance=±5% power=0.25 resistance=10k package=THT]

nets:
  N1: Part1.GND, LED1.anode, LED2.anode, SG1.2, R3.Pin_1
  N2: Part1.D2_PWM, S1.Pin_1, S1.Pin_2
  N3: Part1.D30, R1.Pin_0
  N4: Part1.D32, SG1.1
  N5: Part1.D34, R2.Pin_0
  N6: R1.Pin_1, LED1.cathode
  N7: LED2.cathode, R2.Pin_1

// code stored in the sketch: test.ino
void setup() {
	pinMode(2, OUTPUT);
	digitalWrite(2, HIGH);
}

void loop() {

}
